# Fritzing sketch All (saved by Fritzing 0.9.3b)
breadboards: 2

parts:
  パーツ1 = Arduino Nano (Rev3.0)
  Power_plug1 = Power plug
  IC3 = IC, DIP package, 18 pins [chip_label=IC]
  IC4 = IC, DIP package, 10 pins [chip_label=IC]
  J1 = Basic Servo
  R3 = Photocell (LDR) [package=THT]
  R4 = Resistor [tolerance=±5% resistance=1k package=THT]
  IC5 = IC, DIP package, 16 pins [chip_label=IC]
  C2 = Ceramic Capacitor [capacitance=100nF package="100 mil [THT, multilayer]"]
  C3 = Electrolytic Capacitor [capacitance=1µF package="100 mil [THT, electrolytic]"]
  C4 = Ceramic Capacitor [capacitance=100nF package="100 mil [THT, multilayer]"]
  VCC1 = Battery
  Part1 = XBee Explorer Regulated
  U1 = XBee  # not connected
  M1 = DC Motor
  C11 = Electrolytic Capacitor [capacitance=1µF package="100 mil [THT, electrolytic]"]
  C12 = Ceramic Capacitor [capacitance=100nF package="100 mil [THT, multilayer]"]
  IC6 = PICAXE-08 [package=THT]

nets:
  GND: パーツ1.GND, Power_plug1.GND, IC3.pin13, IC4.pin8, IC4.pin9, J1.gnd, R4.Pin_1, IC5.pin5, C2.0, C3.-, VCC1.-, Part1.GND, C11.-, IC6.In_3
  N1: パーツ1.D2, Part1.DOUT
  N2: パーツ1.D3, Part1.DIN
  N3: パーツ1.D4, J1.pulse
  N4: パーツ1.D7, IC5.pin1
  N5: パーツ1.D8, IC4.pin7
  N6: パーツ1.D9, IC6.Serial_In
  N7: パーツ1.D10, IC3.pin17
  N8: パーツ1.D11/MOSI, IC3.pin16, IC5.pin2
  N9: パーツ1.D12/MISO, IC3.pin15, IC5.pin3
  VIN: パーツ1.VIN, Power_plug1.VCC
  5V: パーツ1.5V, IC3.pin10, IC4.pin10, J1.vcc, R3.pin_0, IC5.pin6, Part1.5V, C11.+, C12.1, IC6.+V
  N10: パーツ1.A5, IC5.pin8
  N11: パーツ1.A4, IC5.pin7
  N12: パーツ1.A3, IC6.In/Out_4
  N13: パーツ1.A1, R3.pin_1, R4.Pin_0
  N14: パーツ1.D13/SCK, IC3.pin14, IC5.pin4
  N15: C2.1, C3.+, VCC1.+
  N16: C4.0, M1.pin_2
  N17: C4.1, M1.pin_1

notes:
  12V
  5V
  3.3V
  SD
  Camera
  GPS
  Servo
  Light
  Barometer
  IMU
  1kΩ
  100uF
  0.1uF
  MotorDriver
  ←
  Xbee
  DC Motor
  Battery for DC motor
  1uF
  Microphone
