# Fritzing sketch UltrasonicDistanceSensor (saved by Fritzing 0.9.3b)
breadboards: 1

parts:
  パーツ1 = Arduino Nano (Rev3.0)
  Power_plug1 = Power plug
  IC2 = IC, DIP package, 10 pins [chip_label=IC]

nets:
  GND: パーツ1.GND, Power_plug1.GND, IC2.pin5
  N1: パーツ1.D9, IC2.pin3
  VIN: パーツ1.VIN, Power_plug1.VCC
  N2: パーツ1.5V, IC2.pin2
  N3: パーツ1.A3, IC2.pin4

notes:
  12V
  5V
